# Fritzing sketch Esquemático_Display_LCD_16x2 (saved by Fritzing 0.9.3b)
breadboards: 1

parts:
  Componente1 = Franzininho WiFi
  U1 = LCD-16X2 [package=lcd-16x2_noholes]
  R1 = TRIMPOT [package=3362u-2]
  R2 = Resistor [tolerance=±5% resistance=220 package="0402 [SMD]"]

nets:
  N1: Componente1.0, U1.RS
  N2: Componente1.1, U1.E
  N3: Componente1.2, U1.DB4
  N4: Componente1.3, U1.DB5
  N5: Componente1.4, U1.DB6
  N6: Componente1.5, U1.DB7
  N7: Componente1.GND, U1.R_W, R1.CCW
  N8: Componente1.5V, U1.A, R1.CW, R2.Pin_0
  N9: U1.VO, R1.WIPER
  N10: U1.K, R2.Pin_1

custom parts:
  Franzininho WiFi: Placa de desenvolvimento ESP32-S2
